# Fritzing sketch VAforAll-Wiring (saved by Fritzing 0.8.3b)
breadboards: 1

parts:
  IC1 = IC, DIP package, 16 pins [chip_label=WTV020 part_number=WTV020]
  Part1 = Arduino Uno (Rev3)
  SP1 = SPEAKER [package=pcb_mount_speaker]  # not connected
  LED1 = LED - 5mm [color="Yellow (595nm)" package="5 mm [THT]"]
  R2 = Resistor [tolerance=±5% resistance=220 package=THT]
  J1 = Basic Servo
  BAT1 = BC9VPC [package=bc9vpc]
  TRS1 = Audio Jack (TRS) 3.5mm [package="4Ucon 08780 [THT]"]

nets:
  N1: IC1.pin4, IC1.pin5, TRS1.Ring, TRS1.Tip
  N2: IC1.pin7, Part1.D3_PWM
  GND: IC1.pin8, Part1.GND, J1.gnd, BAT1.V+
  N3: IC1.pin10, Part1.D6_PWM
  N4: IC1.pin15, Part1.D7, LED1.cathode
  N5: Part1.D9_PWM, J1.pulse
  N6: Part1.3V3, R2.Pin_1
  N7: LED1.anode, R2.Pin_0
  N8: J1.vcc, BAT1.V-

notes:
  Pretend this is your
  MAKEY MAKEY
  pin 14
  Pretend this is your PC
  USB - USB - USB
  Pretend this is your Webcam
  Handle 1
  to 'Click'
  Handle 2
  to 'Earth'
